// Logisim project processor.circ as structural Verilog: 13 circuits, main circuit PROCESSOR
module PROCESSOR (
  output [3:0] icode,
  output [3:0] ifun,
  output [3:0] rA,
  output [3:0] rB,
  output [63:0] valC,
  output [11:0] valP,
  output ZF,
  output SF,
  output OF,
  output [11:0] current_pc,
  output [63:0] rax,
  output [63:0] rcx,
  output [63:0] rdx,
  output [63:0] rbx,
  output [63:0] rsp,
  output [63:0] rbp,
  output [11:0] number_of_steps,
  output [63:0] rsi,
  output [63:0] rdi,
  output [63:0] r8,
  output [63:0] r9,
  output [63:0] r10,
  output [63:0] r11,
  output [63:0] r12,
  output [63:0] r13,
  output [63:0] r14
);

  wire c12, c19, clk, clock_1_out, counter_1_carry, decoder_1_out0, decoder_1_out1, decoder_1_out2,
       decoder_1_out3, decoder_1_out4, decoder_1_out5, decoder_1_out6, decoder_1_out7, decoder_1_out8,
       decoder_1_out9, decoder_1_out10, decoder_1_out11, decoder_1_out13, decoder_1_out14, decoder_1_out15,
       decoder_1_out16, decoder_1_out17, decoder_1_out18, decoder_1_out20, decoder_1_out21, decoder_1_out22,
       decoder_1_out23, decoder_1_out24, execute_1_cond_out, fetch_1_halt, not_1_out,
       set_data_and_address_1_read, set_data_and_address_1_write;
  wire [3:0] set_sources_and_destinations_1_dste, set_sources_and_destinations_1_dstm,
       set_sources_and_destinations_1_srca, set_sources_and_destinations_1_srcb;
  wire [7:0] ct;
  wire [11:0] counter_2_q, multiplexer_1_out, update_1_new_pc;
  wire [63:0] execute_1_vale, execute_1_vale_for_memory, memory_1_valm, register_file_1_vala,
       register_file_1_valb, set_data_and_address_1_address, set_data_and_address_1_data;

  not not_1 (not_1_out, fetch_1_halt);
  Clock clock_1 (.out(clock_1_out));
  assign clk = not_1_out ? clock_1_out : 1'bz;  // Controlled_Buffer controlled_buffer_1
  Counter #(.max('h18)) counter_1 (.Q(ct), .carry(counter_1_carry), .clk(clk));  // open: load, D, count, up, clr
  Counter #(.max('hfff), .width(12)) counter_2 (
    .Q(counter_2_q), .clk(counter_1_carry));  // open: load, D, count, carry, up, clr
  LED led_1 (.in(decoder_1_out0));
  LED led_2 (.in(decoder_1_out1));
  LED led_3 (.in(decoder_1_out2));
  LED led_4 (.in(decoder_1_out3));
  LED led_5 (.in(decoder_1_out4));
  LED led_6 (.in(decoder_1_out5));
  LED led_7 (.in(decoder_1_out6));
  Decoder #(.enable("false"), .select(5)) decoder_1 (
    .out0(decoder_1_out0), .out1(decoder_1_out1), .out2(decoder_1_out2), .out3(decoder_1_out3),
    .out4(decoder_1_out4), .out5(decoder_1_out5), .out6(decoder_1_out6), .out7(decoder_1_out7),
    .out8(decoder_1_out8), .out9(decoder_1_out9), .out10(decoder_1_out10), .out11(decoder_1_out11),
    .out12(c12), .out13(decoder_1_out13), .out14(decoder_1_out14), .out15(decoder_1_out15),
    .out16(decoder_1_out16), .out17(decoder_1_out17), .out18(decoder_1_out18), .out19(c19),
    .out20(decoder_1_out20), .out21(decoder_1_out21), .out22(decoder_1_out22), .out23(decoder_1_out23),
    .out24(decoder_1_out24), .sel(ct[4:0]));  // open: out25, out26, out27, out28, out29, out30, out31
  FETCH fetch_1 (
    .clk(clk), .PC(current_pc), .HALT(fetch_1_halt), .rA(rA), .rB(rB), .icode(icode), .ifun(ifun),
    .valC(valC), .valP(valP));
  Register #(.width(12)) register_1 (.D(multiplexer_1_out), .clk(clk), .Q(current_pc));  // open: en, clr
  Multiplexer #(.width(12)) multiplexer_1 (
    .in0(current_pc), .in1(update_1_new_pc), .out(multiplexer_1_out), .sel(counter_1_carry));
  Adder #(.width(12)) adder_1 (.a(12'h1), .b(counter_2_q), .out(number_of_steps));  // open: cin, cout
  LED led_8 (.in(decoder_1_out7));
  LED led_9 (.in(decoder_1_out8));
  LED led_10 (.in(decoder_1_out9));
  LED led_11 (.in(decoder_1_out10));
  LED led_12 (.in(decoder_1_out11));
  LED led_13 (.in(decoder_1_out13));
  LED led_14 (.in(decoder_1_out14));
  LED led_15 (.in(decoder_1_out15));
  LED led_16 (.in(decoder_1_out16));
  LED led_17 (.in(decoder_1_out17));
  LED led_18 (.in(decoder_1_out18));
  LED led_19 (.in(decoder_1_out20));
  LED led_20 (.in(decoder_1_out21));
  LED led_21 (.in(decoder_1_out22));
  REGISTER_FILE register_file_1 (
    .clk(clk), .srcA(set_sources_and_destinations_1_srca), .srcB(set_sources_and_destinations_1_srcb),
    .load_next_in(c19), .dstE(set_sources_and_destinations_1_dste),
    .dstM(set_sources_and_destinations_1_dstm), .valE(execute_1_vale), .valM(memory_1_valm), .icode(icode),
    .ValB(register_file_1_valb), .ValA(register_file_1_vala), .rax(rax), .rcx(rcx), .rdx(rdx), .rbx(rbx),
    .rsp(rsp), .rbp(rbp), .rsi(rsi), .rdi(rdi), .r8(r8), .r9(r9), .r10(r10), .r11(r11), .r12(r12), .r13(r13),
    .r14(r14));
  set_sources_and_destinations set_sources_and_destinations_1 (
    .rA(rA), .rB(rB), .icode(icode), .srcA(set_sources_and_destinations_1_srca),
    .srcB(set_sources_and_destinations_1_srcb), .dstE(set_sources_and_destinations_1_dste),
    .dstM(set_sources_and_destinations_1_dstm));
  LED led_22 (.in(decoder_1_out23));
  LED led_23 (.in(decoder_1_out24));
  set_data_and_address set_data_and_address_1 (
    .valE(execute_1_vale_for_memory), .valA(register_file_1_vala), .icode(icode), .ct(ct),
    .write(set_data_and_address_1_write), .address(set_data_and_address_1_address),
    .data(set_data_and_address_1_data), .read(set_data_and_address_1_read));
  MEMORY memory_1 (
    .write_enable(set_data_and_address_1_write), .mem_data(set_data_and_address_1_data),
    .mem_address(set_data_and_address_1_address), .clk(clk), .read_enable(set_data_and_address_1_read),
    .valM(memory_1_valm));
  EXECUTE execute_1 (
    .valA(register_file_1_vala), .valC(valC), .icode(icode), .ifun(ifun), .valB(register_file_1_valb),
    .count12(c12), .clk(clk), .valE(execute_1_vale), .valE_for_memory(execute_1_vale_for_memory), .ZF(ZF),
    .SF(SF), .OverF(OF), .cond_out(execute_1_cond_out));
  UPDATE update_1 (.valC(valC), .Cnd(execute_1_cond_out), .valP(valP), .icode(icode), .new_pc(update_1_new_pc));

  // Notes on the sheet:
  //   current clock cycle
  //   (counts to 24)
  //   set srcA, srcB, dstE, dstM
  //   this processor does not have the following instructions available: cmov, call, ret
  //   set read, write, addr, data
endmodule

module FETCH (
  input  [11:0] PC,
  input  clk,
  output [3:0] icode,
  output [3:0] ifun,
  output HALT,
  output [3:0] rA,
  output [3:0] rB,
  output [63:0] valC,
  output [11:0] valP
);

  wire clock_1_out, clock_2_out, clock_3_out, clock_4_out, clock_5_out, clock_6_out, clock_7_out,
       clock_8_out, clock_9_out, clock_10_out, comparator_1_eq, comparator_2_eq, deciding_logic_1_load0,
       deciding_logic_1_load1, deciding_logic_1_load2, deciding_logic_1_load3, deciding_logic_1_load4,
       deciding_logic_1_load5, deciding_logic_1_load6, deciding_logic_1_load7, deciding_logic_1_load8,
       deciding_logic_1_load9, deciding_logic_1_load_new;
  wire [7:0] instruction_source_1_out_4, multiplexer_1_out, multiplexer_2_out, multiplexer_3_out,
       multiplexer_4_out, multiplexer_5_out, multiplexer_6_out, multiplexer_7_out, multiplexer_8_out,
       multiplexer_9_out, multiplexer_10_out;

  instruction_source instruction_source_1 (
    .clk(clk), .PC(PC), .load_pc(deciding_logic_1_load_new), .out_4(instruction_source_1_out_4));
  deciding_logic deciding_logic_1 (
    .icode(icode), .clk(clk), .load1(deciding_logic_1_load1), .load2(deciding_logic_1_load2),
    .load3(deciding_logic_1_load3), .load4(deciding_logic_1_load4), .load5(deciding_logic_1_load5),
    .load6(deciding_logic_1_load6), .load7(deciding_logic_1_load7), .load8(deciding_logic_1_load8),
    .load9(deciding_logic_1_load9), .load_new(deciding_logic_1_load_new), .load0(deciding_logic_1_load0));
  pc_increment_logic pc_increment_logic_1 (.icode(icode), .current_pc(PC), .ValP(valP));
  Register register_1 (
    .D(multiplexer_1_out), .en(deciding_logic_1_load0), .clk(clock_1_out), .Q({icode, ifun}));  // open: clr
  Multiplexer #(.width(8)) multiplexer_1 (
    .in0({icode, ifun}), .in1(instruction_source_1_out_4), .out(multiplexer_1_out),
    .sel(deciding_logic_1_load0));
  Clock clock_1 (.out(clock_1_out));
  Register register_2 (.D(multiplexer_2_out), .clk(clock_2_out), .Q({rA, rB}));  // open: en, clr
  Multiplexer #(.width(8)) multiplexer_2 (
    .in0({rA, rB}), .in1(instruction_source_1_out_4), .out(multiplexer_2_out), .sel(deciding_logic_1_load1));
  Clock clock_2 (.out(clock_2_out));
  Multiplexer #(.width(8)) multiplexer_3 (
    .in0(valC[7:0]), .in1(instruction_source_1_out_4), .out(multiplexer_3_out), .sel(deciding_logic_1_load2));
  Multiplexer #(.width(8)) multiplexer_4 (
    .in0(valC[15:8]), .in1(instruction_source_1_out_4), .out(multiplexer_4_out), .sel(deciding_logic_1_load3));
  Multiplexer #(.width(8)) multiplexer_5 (
    .in0(valC[23:16]), .in1(instruction_source_1_out_4), .out(multiplexer_5_out), .sel(deciding_logic_1_load4));
  Multiplexer #(.width(8)) multiplexer_6 (
    .in0(valC[31:24]), .in1(instruction_source_1_out_4), .out(multiplexer_6_out), .sel(deciding_logic_1_load5));
  Multiplexer #(.width(8)) multiplexer_7 (
    .in0(valC[39:32]), .in1(instruction_source_1_out_4), .out(multiplexer_7_out), .sel(deciding_logic_1_load6));
  Multiplexer #(.width(8)) multiplexer_8 (
    .in0(valC[47:40]), .in1(instruction_source_1_out_4), .out(multiplexer_8_out), .sel(deciding_logic_1_load7));
  Multiplexer #(.width(8)) multiplexer_9 (
    .in0(valC[55:48]), .in1(instruction_source_1_out_4), .out(multiplexer_9_out), .sel(deciding_logic_1_load8));
  Multiplexer #(.width(8)) multiplexer_10 (
    .in0(valC[63:56]), .in1(instruction_source_1_out_4), .out(multiplexer_10_out),
    .sel(deciding_logic_1_load9));
  Register register_3 (.D(multiplexer_3_out), .clk(clock_3_out), .Q(valC[7:0]));  // open: en, clr
  Clock clock_3 (.out(clock_3_out));
  Register register_4 (.D(multiplexer_4_out), .clk(clock_4_out), .Q(valC[15:8]));  // open: en, clr
  Clock clock_4 (.out(clock_4_out));
  Register register_5 (.D(multiplexer_5_out), .clk(clock_5_out), .Q(valC[23:16]));  // open: en, clr
  Clock clock_5 (.out(clock_5_out));
  Register register_6 (.D(multiplexer_6_out), .clk(clock_6_out), .Q(valC[31:24]));  // open: en, clr
  Clock clock_6 (.out(clock_6_out));
  Register register_7 (.D(multiplexer_7_out), .clk(clock_7_out), .Q(valC[39:32]));  // open: en, clr
  Clock clock_7 (.out(clock_7_out));
  Register register_8 (.D(multiplexer_8_out), .clk(clock_8_out), .Q(valC[47:40]));  // open: en, clr
  Clock clock_8 (.out(clock_8_out));
  Register register_9 (.D(multiplexer_9_out), .clk(clock_9_out), .Q(valC[55:48]));  // open: en, clr
  Clock clock_9 (.out(clock_9_out));
  Register register_10 (.D(multiplexer_10_out), .clk(clock_10_out), .Q(valC[63:56]));  // open: en, clr
  Clock clock_10 (.out(clock_10_out));
  Comparator #(.width(4)) comparator_1 (.a(icode), .b(4'b0000), .eq(comparator_1_eq));  // open: gt, lt
  and and_1 (HALT, comparator_1_eq, comparator_2_eq);
  Comparator #(.width(4)) comparator_2 (.a(ifun), .b(4'b0000), .eq(comparator_2_eq));  // open: gt, lt

  // Notes on the sheet:
  //   <-
  //   Deciding
  //   Logic
  //   load_new
  //   clk
  //   icode
  //   PC Increment
  //   Logic
  //   0
  //   1
  //   2
  //   3
  //   4
  //   5
  //   6
  //   7
  //   8
  //   9
  //   icode
  //   (4 bits)
  //   (4 bits)
  //   (4 bits)
  //   (4 bits)
  //   (12 bits)
  //   (64 bits)
endmodule

module instruction_source (
  input  load_pc,
  input  clk,
  input  [11:0] PC,
  output [7:0] out_4
);

  wire [11:0] counter_1_q;

  Counter #(.max('hfff), .width(12)) counter_1 (
    .load(load_pc), .clk(clk), .D(PC), .Q(counter_1_q));  // open: clr, up, count, carry
  ROM #(.addrWidth(12)) rom_1 (.addr(counter_1_q), .data(out_4));

  // Notes on the sheet:
  //   contents of rom_1 (hex, n*v repeats v):
  //   30 f0 4 7*0 30 f1 b 7*0 30 f2 36 7*0 30 f3 47 7*0 30 f4 0 7 6*0 30 f5 5d 7*0 30 f6 18 7*0 30 f7 41
  //   7*0 30 f8 50 7*0 30 f9 0 1 6*0 30 fa 50 1 6*0 30 fb 0 2 6*0 30 fc 50 2 6*0 30 fd 0 3 6*0 30 fe 50 3
  //   6*0 10 62 63 63 75 60 65 61 6 63 1 61 2 60 31 61 62 60 70 62 25 60 6 62 57 63 15 62 60 63 71 20 13
  //   40 b 8*0 40 1c 8*0 50 5c 8*0 20 76 40 6e 8*0 30 f2 43 7*0 40 5a 8*0 30 f5 7 7*0 50 7a 8*0 a0 5f b0 f
  //   a0 7f 60 60 b0 f 30 f7 33 7*0 63 75 62 63 30 f5 b 7*0 40 5d 8*0 61 6 50 1d 8*0 70 5e 1 6*0 30 f0 f
  //   7*0 30 f5 f 7*0 20 50 62 25 76 6d 1 6*0 20 13 20 16 62 20 72 7e 1 6*0 63 60 61 17 60 66 20 67 75 8f
  //   1 6*0 60 67 62 5 60 62 63 25 71 a0 1 6*0 63 52 61 57 63 52 62 1 73 b3 1 6*0 61 67 63 71 62 3 63 75
  //   61 60 30 f5 e 7*0 74 ce 1 6*0 60 62 63 6 63 76 60 62 20 65
endmodule

module deciding_logic (
  input  [3:0] icode,
  input  clk,
  output load0,
  output load1,
  output load2,
  output load3,
  output load4,
  output load5,
  output load6,
  output load7,
  output load8,
  output load9,
  output load_new
);

  wire and_1_out, and_2_out, and_3_out, decoder_1_out0, decoder_1_out1, decoder_1_out2, decoder_1_out6,
       decoder_1_out7, decoder_1_out10, decoder_1_out11, decoder_2_out1, decoder_2_out2, decoder_2_out3,
       decoder_2_out4, decoder_2_out5, decoder_2_out6, decoder_2_out7, decoder_2_out8, decoder_2_out9,
       demultiplexer_1_out1, demultiplexer_2_out0, demultiplexer_2_out1, demultiplexer_3_out0,
       demultiplexer_3_out1, demultiplexer_4_out0, demultiplexer_4_out1, demultiplexer_5_out0,
       demultiplexer_5_out1, demultiplexer_6_out0, demultiplexer_6_out1, demultiplexer_7_out0,
       demultiplexer_7_out1, demultiplexer_8_out0, demultiplexer_8_out1, demultiplexer_9_out0, or_1_out,
       or_2_out;
  wire [3:0] and_4_out, counter_1_q, not_1_out;

  or or_1 (or_1_out, decoder_1_out0, decoder_1_out1);
  and and_1 (and_1_out, or_1_out, load0);
  or or_2 (or_2_out, decoder_1_out11, decoder_1_out10, decoder_1_out6, decoder_1_out2);
  and and_2 (and_2_out, or_2_out, decoder_2_out1);
  and and_3 (and_3_out, decoder_1_out7, decoder_2_out8);
  or or_3 (load_new, and_1_out, and_2_out, and_3_out, decoder_2_out9);
  Decoder #(.enable("false"), .select(4)) decoder_1 (
    .out0(decoder_1_out0), .out1(decoder_1_out1), .out2(decoder_1_out2), .out6(decoder_1_out6),
    .out7(decoder_1_out7), .out10(decoder_1_out10), .out11(decoder_1_out11), .sel(icode));  // open: out3, out4, out5, out8, out9, out12, out13, out14, out15
  assign and_4_out = counter_1_q & not_1_out;  // AND_Gate and_4, 4 bits wide
  assign not_1_out = ~counter_1_q;  // NOT_Gate not_1, 4 bits wide
  Counter #(.max('h9), .width(4)) counter_1 (
    .load(load_new), .clk(clk), .D(and_4_out), .Q(counter_1_q));  // open: clr, up, count, carry
  Decoder #(.enable("false"), .select(4)) decoder_2 (
    .out0(load0), .out1(decoder_2_out1), .out2(decoder_2_out2), .out3(decoder_2_out3), .out4(decoder_2_out4),
    .out5(decoder_2_out5), .out6(decoder_2_out6), .out7(decoder_2_out7), .out8(decoder_2_out8),
    .out9(decoder_2_out9), .sel(counter_1_q));  // open: out10, out11, out12, out13, out14, out15
  Demultiplexer demultiplexer_1 (.out0(load1), .out1(demultiplexer_1_out1), .in(decoder_2_out1), .sel(decoder_1_out7));
  Demultiplexer demultiplexer_2 (
    .out0(demultiplexer_2_out0), .out1(demultiplexer_2_out1), .in(decoder_2_out2), .sel(decoder_1_out7));
  Demultiplexer demultiplexer_3 (
    .out0(demultiplexer_3_out0), .out1(demultiplexer_3_out1), .in(decoder_2_out3), .sel(decoder_1_out7));
  Demultiplexer demultiplexer_4 (
    .out0(demultiplexer_4_out0), .out1(demultiplexer_4_out1), .in(decoder_2_out4), .sel(decoder_1_out7));
  Demultiplexer demultiplexer_5 (
    .out0(demultiplexer_5_out0), .out1(demultiplexer_5_out1), .in(decoder_2_out5), .sel(decoder_1_out7));
  Demultiplexer demultiplexer_6 (
    .out0(demultiplexer_6_out0), .out1(demultiplexer_6_out1), .in(decoder_2_out6), .sel(decoder_1_out7));
  Demultiplexer demultiplexer_7 (
    .out0(demultiplexer_7_out0), .out1(demultiplexer_7_out1), .in(decoder_2_out7), .sel(decoder_1_out7));
  Demultiplexer demultiplexer_8 (
    .out0(demultiplexer_8_out0), .out1(demultiplexer_8_out1), .in(decoder_2_out8), .sel(decoder_1_out7));
  Demultiplexer demultiplexer_9 (.out0(demultiplexer_9_out0), .in(decoder_2_out9), .sel(decoder_1_out7));  // open: out1
  or or_4 (load2, demultiplexer_1_out1, demultiplexer_2_out0);
  or or_5 (load3, demultiplexer_2_out1, demultiplexer_3_out0);
  or or_6 (load4, demultiplexer_3_out1, demultiplexer_4_out0);
  or or_7 (load5, demultiplexer_4_out1, demultiplexer_5_out0);
  or or_8 (load6, demultiplexer_5_out1, demultiplexer_6_out0);
  or or_9 (load7, demultiplexer_6_out1, demultiplexer_7_out0);
  or or_10 (load8, demultiplexer_7_out1, demultiplexer_8_out0);
  or or_11 (load9, demultiplexer_8_out1, demultiplexer_9_out0);

  // Notes on the sheet:
  //   icode = 0+1
  //   and count = 0
  //   icode = 2+6+A+B
  //   and count = 1
  //   icode = 7
  //   and count = 8
  //   count = 9
endmodule

module pc_increment_logic (
  input  [3:0] icode,
  input  [11:0] current_pc,
  output [11:0] ValP
);

  wire decoder_1_out2, decoder_1_out3, decoder_1_out4, decoder_1_out5, decoder_1_out6, decoder_1_out7,
       decoder_1_out8, decoder_1_out10, decoder_1_out11, or_1_out, or_2_out;
  wire [11:0] adder_1_out, adder_2_out, multiplexer_1_out, multiplexer_2_out;

  Decoder #(.enable("false"), .select(4)) decoder_1 (
    .out2(decoder_1_out2), .out3(decoder_1_out3), .out4(decoder_1_out4), .out5(decoder_1_out5),
    .out6(decoder_1_out6), .out7(decoder_1_out7), .out8(decoder_1_out8), .out10(decoder_1_out10),
    .out11(decoder_1_out11), .sel(icode));  // open: out0, out1, out9, out12, out13, out14, out15
  Adder #(.width(12)) adder_1 (.a(12'h1), .b(current_pc), .out(adder_1_out));  // open: cin, cout
  or or_1 (or_1_out, decoder_1_out2, decoder_1_out3, decoder_1_out4, decoder_1_out5, decoder_1_out6, decoder_1_out10, decoder_1_out11);
  Multiplexer #(.width(12)) multiplexer_1 (.in0({12{1'b0}}), .in1(12'h1), .out(multiplexer_1_out), .sel(or_1_out));
  or or_2 (or_2_out, decoder_1_out8, decoder_1_out7, decoder_1_out3, decoder_1_out4, decoder_1_out5);
  Adder #(.width(12)) adder_2 (.a(multiplexer_1_out), .b(adder_1_out), .out(adder_2_out));  // open: cin, cout
  Multiplexer #(.width(12)) multiplexer_2 (.in0({12{1'b0}}), .in1(12'h8), .out(multiplexer_2_out), .sel(or_2_out));
  Adder #(.width(12)) adder_3 (.a(multiplexer_2_out), .b(adder_2_out), .out(ValP));  // open: cin, cout

  // Notes on the sheet:
  //   Add 1 (all)
  //   Add 1 (instructions 2,3,4,5,6,10,11)
  //   Add 8 (instructions 3,4,5,7,8)
endmodule

module REGISTER_FILE (
  input  [3:0] icode,
  input  clk,
  input  [3:0] dstE,
  input  [3:0] srcA,
  input  load_next_in,
  input  [63:0] valE,
  input  [63:0] valM,
  input  [3:0] srcB,
  input  [3:0] dstM,
  output [63:0] ValA,
  output [63:0] ValB,
  output [63:0] rax,
  output [63:0] rcx,
  output [63:0] rdx,
  output [63:0] rbx,
  output [63:0] rsp,
  output [63:0] rbp,
  output [63:0] rsi,
  output [63:0] rdi,
  output [63:0] r8,
  output [63:0] r9,
  output [63:0] r10,
  output [63:0] r11,
  output [63:0] r12,
  output [63:0] r13,
  output [63:0] r14
);

  wire decoder_1_out2, decoder_1_out3, decoder_1_out6, decoder_1_out8, decoder_1_out9, decoder_1_out10,
       decoder_1_out11, decoder_2_p2, decoder_2_p7, decoder_5_out0, decoder_5_out1, decoder_5_out2,
       decoder_5_out3, decoder_5_out4, decoder_5_out5, decoder_5_out6, decoder_5_out7, decoder_5_out8,
       decoder_5_out9, decoder_5_out10, decoder_5_out11, decoder_5_out12, decoder_5_out13, decoder_5_out14,
       decoder_6_out0, decoder_6_out1, decoder_6_out2, decoder_6_out3, decoder_6_out4, decoder_6_out5,
       decoder_6_out6, decoder_6_out7, decoder_6_out8, decoder_6_out9, decoder_6_out10, decoder_6_out11,
       decoder_6_out12, decoder_6_out13, decoder_6_out14, decoder_7_out2, decoder_7_out4, decoder_7_out6,
       decoder_7_out10, decoder_8_out4, decoder_8_out5, decoder_8_out6, decoder_8_out10, decoder_8_out11,
       or_1_out, or_2_out, or_3_out, or_4_out;
  wire [1:0] decoder_2_p3, decoder_2_p4, decoder_2_p5, decoder_2_p6, decoder_2_p8, decoder_2_p9,
       decoder_2_p10, decoder_2_p11, decoder_2_p12, decoder_2_p13, decoder_2_p14, decoder_3_out0,
       decoder_3_out1, decoder_3_out2, decoder_3_out3;
  wire [3:0] multiplexer_1_out, multiplexer_2_out, multiplexer_18_out, multiplexer_19_out;
  wire [63:0] multiplexer_3_out, multiplexer_4_out, multiplexer_5_out, multiplexer_6_out, multiplexer_7_out,
       multiplexer_8_out, multiplexer_9_out, multiplexer_10_out, multiplexer_11_out, multiplexer_12_out,
       multiplexer_13_out, multiplexer_14_out, multiplexer_15_out, multiplexer_16_out, multiplexer_17_out;

  Decoder #(.enable("false"), .select(4)) decoder_1 (
    .out2(decoder_1_out2), .out3(decoder_1_out3), .out6(decoder_1_out6), .out8(decoder_1_out8),
    .out9(decoder_1_out9), .out10(decoder_1_out10), .out11(decoder_1_out11), .sel(icode));  // open: out0, out1, out4, out5, out7, out12, out13, out14, out15
  or or_1 (or_1_out, decoder_1_out2, decoder_1_out3, decoder_1_out6, decoder_1_out8, decoder_1_out9, decoder_1_out10, decoder_1_out11);
  Multiplexer #(.width(4)) multiplexer_1 (.in0(4'b1111), .in1(dstE), .out(multiplexer_1_out), .sel(or_1_out));
  // Decoder #(.enable("false"), .select(4)) decoder_2: pin names not known; wires that end beside it: icode, decoder_2_p2, decoder_2_p3[0], decoder_2_p4[0], decoder_2_p5[0], decoder_2_p6[0], decoder_2_p7, decoder_2_p8[0], decoder_2_p9[0], decoder_2_p10[0], decoder_2_p11[0], decoder_2_p12[0], decoder_2_p13[0], decoder_2_p14[0]
  Decoder #(.enable("false"), .select(4)) decoder_3 (
    .out0(decoder_3_out0[0]), .out1(decoder_3_out1[0]), .out2(decoder_3_out2[0]), .out3(decoder_3_out3[0]),
    .out4(decoder_2_p14[0]), .out5(decoder_2_p13[0]), .out6(decoder_2_p12[0]), .out7(decoder_2_p11[0]),
    .out8(decoder_2_p10[0]), .out9(decoder_2_p9[0]), .out10(decoder_2_p8[0]), .out11(decoder_2_p6[0]),
    .out12(decoder_2_p5[0]), .out13(decoder_2_p4[0]), .out14(decoder_2_p3[0]), .sel(multiplexer_1_out));  // open: out15
  or or_2 (or_2_out, decoder_2_p2, decoder_2_p7);
  Multiplexer #(.width(4)) multiplexer_2 (.in0(4'b1111), .in1(dstM), .out(multiplexer_2_out), .sel(or_2_out));
  Decoder #(.enable("false"), .select(4)) decoder_4 (
    .out0(decoder_3_out0[1]), .out1(decoder_3_out1[1]), .out2(decoder_3_out2[1]), .out3(decoder_3_out3[1]),
    .out4(decoder_2_p14[1]), .out5(decoder_2_p13[1]), .out6(decoder_2_p12[1]), .out7(decoder_2_p11[1]),
    .out8(decoder_2_p10[1]), .out9(decoder_2_p9[1]), .out10(decoder_2_p8[1]), .out11(decoder_2_p6[1]),
    .out12(decoder_2_p5[1]), .out13(decoder_2_p4[1]), .out14(decoder_2_p3[1]), .sel(multiplexer_2_out));  // open: out15
  Register #(.width(64)) register_1 (.D(multiplexer_3_out), .en(load_next_in), .clk(clk), .Q(rax));  // open: clr
  Multiplexer #(.select(2), .width(64)) multiplexer_3 (
    .in0(rax), .in1(valE), .in2(valM), .in3(rax), .out(multiplexer_3_out), .sel(decoder_3_out0));
  Register #(.width(64)) register_2 (.D(multiplexer_4_out), .en(load_next_in), .clk(clk), .Q(rcx));  // open: clr
  Multiplexer #(.select(2), .width(64)) multiplexer_4 (
    .in0(rcx), .in1(valE), .in2(valM), .in3(rcx), .out(multiplexer_4_out), .sel(decoder_3_out1));
  Register #(.width(64)) register_3 (.D(multiplexer_5_out), .en(load_next_in), .clk(clk), .Q(rdx));  // open: clr
  Multiplexer #(.select(2), .width(64)) multiplexer_5 (
    .in0(rdx), .in1(valE), .in2(valM), .in3(rdx), .out(multiplexer_5_out), .sel(decoder_3_out2));
  Register #(.width(64)) register_4 (.D(multiplexer_6_out), .en(load_next_in), .clk(clk), .Q(rbx));  // open: clr
  Multiplexer #(.select(2), .width(64)) multiplexer_6 (
    .in0(rbx), .in1(valE), .in2(valM), .in3(rbx), .out(multiplexer_6_out), .sel(decoder_3_out3));
  Register #(.width(64)) register_5 (.D(multiplexer_7_out), .en(load_next_in), .clk(clk), .Q(rsp));  // open: clr
  Multiplexer #(.select(2), .width(64)) multiplexer_7 (
    .in0(rsp), .in1(valE), .in2(valM), .in3(rsp), .out(multiplexer_7_out), .sel(decoder_2_p14));
  Register #(.width(64)) register_6 (.D(multiplexer_8_out), .en(load_next_in), .clk(clk), .Q(rbp));  // open: clr
  Multiplexer #(.select(2), .width(64)) multiplexer_8 (
    .in0(rbp), .in1(valE), .in2(valM), .in3(rbp), .out(multiplexer_8_out), .sel(decoder_2_p13));
  Register #(.width(64)) register_7 (.D(multiplexer_9_out), .en(load_next_in), .clk(clk), .Q(rsi));  // open: clr
  Multiplexer #(.select(2), .width(64)) multiplexer_9 (
    .in0(rsi), .in1(valE), .in2(valM), .in3(rsi), .out(multiplexer_9_out), .sel(decoder_2_p12));
  Register #(.width(64)) register_8 (.D(multiplexer_10_out), .en(load_next_in), .clk(clk), .Q(rdi));  // open: clr
  Multiplexer #(.select(2), .width(64)) multiplexer_10 (
    .in0(rdi), .in1(valE), .in2(valM), .in3(rdi), .out(multiplexer_10_out), .sel(decoder_2_p11));
  Register #(.width(64)) register_9 (.D(multiplexer_11_out), .en(load_next_in), .clk(clk), .Q(r8));  // open: clr
  Multiplexer #(.select(2), .width(64)) multiplexer_11 (
    .in0(r8), .in1(valE), .in2(valM), .in3(r8), .out(multiplexer_11_out), .sel(decoder_2_p10));
  Register #(.width(64)) register_10 (.D(multiplexer_12_out), .en(load_next_in), .clk(clk), .Q(r9));  // open: clr
  Multiplexer #(.select(2), .width(64)) multiplexer_12 (
    .in0(r9), .in1(valE), .in2(valM), .in3(r9), .out(multiplexer_12_out), .sel(decoder_2_p9));
  Register #(.width(64)) register_11 (.D(multiplexer_13_out), .en(load_next_in), .clk(clk), .Q(r10));  // open: clr
  Multiplexer #(.select(2), .width(64)) multiplexer_13 (
    .in0(r10), .in1(valE), .in2(valM), .in3(r10), .out(multiplexer_13_out), .sel(decoder_2_p8));
  Register #(.width(64)) register_12 (.D(multiplexer_14_out), .en(load_next_in), .clk(clk), .Q(r11));  // open: clr
  Multiplexer #(.select(2), .width(64)) multiplexer_14 (
    .in0(r11), .in1(valE), .in2(valM), .in3(r11), .out(multiplexer_14_out), .sel(decoder_2_p6));
  Register #(.width(64)) register_13 (.D(multiplexer_15_out), .en(load_next_in), .clk(clk), .Q(r12));  // open: clr
  Multiplexer #(.select(2), .width(64)) multiplexer_15 (
    .in0(r12), .in1(valE), .in2(valM), .in3(r12), .out(multiplexer_15_out), .sel(decoder_2_p5));
  Register #(.width(64)) register_14 (.D(multiplexer_16_out), .en(load_next_in), .clk(clk), .Q(r13));  // open: clr
  Multiplexer #(.select(2), .width(64)) multiplexer_16 (
    .in0(r13), .in1(valE), .in2(valM), .in3(r13), .out(multiplexer_16_out), .sel(decoder_2_p4));
  Register #(.width(64)) register_15 (.D(multiplexer_17_out), .en(load_next_in), .clk(clk), .Q(r14));  // open: clr
  Multiplexer #(.select(2), .width(64)) multiplexer_17 (
    .in0(r14), .in1(valE), .in2(valM), .in3(r14), .out(multiplexer_17_out), .sel(decoder_2_p3));
  assign ValA = decoder_5_out0 ? rax : 64'bz;  // Controlled_Buffer controlled_buffer_1
  assign ValA = decoder_5_out1 ? rcx : 64'bz;  // Controlled_Buffer controlled_buffer_2
  assign ValA = decoder_5_out2 ? rdx : 64'bz;  // Controlled_Buffer controlled_buffer_3
  assign ValA = decoder_5_out3 ? rbx : 64'bz;  // Controlled_Buffer controlled_buffer_4
  assign ValA = decoder_5_out4 ? rsp : 64'bz;  // Controlled_Buffer controlled_buffer_5
  assign ValA = decoder_5_out5 ? rbp : 64'bz;  // Controlled_Buffer controlled_buffer_6
  assign ValA = decoder_5_out6 ? rsi : 64'bz;  // Controlled_Buffer controlled_buffer_7
  assign ValA = decoder_5_out7 ? rdi : 64'bz;  // Controlled_Buffer controlled_buffer_8
  assign ValA = decoder_5_out8 ? r8 : 64'bz;  // Controlled_Buffer controlled_buffer_9
  assign ValA = decoder_5_out9 ? r9 : 64'bz;  // Controlled_Buffer controlled_buffer_10
  assign ValA = decoder_5_out10 ? r10 : 64'bz;  // Controlled_Buffer controlled_buffer_11
  assign ValA = decoder_5_out11 ? r11 : 64'bz;  // Controlled_Buffer controlled_buffer_12
  assign ValA = decoder_5_out12 ? r12 : 64'bz;  // Controlled_Buffer controlled_buffer_13
  assign ValA = decoder_5_out13 ? r13 : 64'bz;  // Controlled_Buffer controlled_buffer_14
  assign ValA = decoder_5_out14 ? r14 : 64'bz;  // Controlled_Buffer controlled_buffer_15
  assign ValB = decoder_6_out0 ? rax : 64'bz;  // Controlled_Buffer controlled_buffer_16
  assign ValB = decoder_6_out1 ? rcx : 64'bz;  // Controlled_Buffer controlled_buffer_17
  assign ValB = decoder_6_out2 ? rdx : 64'bz;  // Controlled_Buffer controlled_buffer_18
  assign ValB = decoder_6_out3 ? rbx : 64'bz;  // Controlled_Buffer controlled_buffer_19
  assign ValB = decoder_6_out4 ? rsp : 64'bz;  // Controlled_Buffer controlled_buffer_20
  assign ValB = decoder_6_out5 ? rbp : 64'bz;  // Controlled_Buffer controlled_buffer_21
  assign ValB = decoder_6_out6 ? rsi : 64'bz;  // Controlled_Buffer controlled_buffer_22
  assign ValB = decoder_6_out7 ? rdi : 64'bz;  // Controlled_Buffer controlled_buffer_23
  assign ValB = decoder_6_out8 ? r8 : 64'bz;  // Controlled_Buffer controlled_buffer_24
  assign ValB = decoder_6_out9 ? r9 : 64'bz;  // Controlled_Buffer controlled_buffer_25
  assign ValB = decoder_6_out10 ? r10 : 64'bz;  // Controlled_Buffer controlled_buffer_26
  assign ValB = decoder_6_out11 ? r11 : 64'bz;  // Controlled_Buffer controlled_buffer_27
  assign ValB = decoder_6_out12 ? r12 : 64'bz;  // Controlled_Buffer controlled_buffer_28
  assign ValB = decoder_6_out13 ? r13 : 64'bz;  // Controlled_Buffer controlled_buffer_29
  assign ValB = decoder_6_out14 ? r14 : 64'bz;  // Controlled_Buffer controlled_buffer_30
  Decoder #(.enable("false"), .select(4)) decoder_5 (
    .out0(decoder_5_out0), .out1(decoder_5_out1), .out2(decoder_5_out2), .out3(decoder_5_out3),
    .out4(decoder_5_out4), .out5(decoder_5_out5), .out6(decoder_5_out6), .out7(decoder_5_out7),
    .out8(decoder_5_out8), .out9(decoder_5_out9), .out10(decoder_5_out10), .out11(decoder_5_out11),
    .out12(decoder_5_out12), .out13(decoder_5_out13), .out14(decoder_5_out14), .sel(multiplexer_18_out));  // open: out15
  Decoder #(.enable("false"), .select(4)) decoder_6 (
    .out0(decoder_6_out0), .out1(decoder_6_out1), .out2(decoder_6_out2), .out3(decoder_6_out3),
    .out4(decoder_6_out4), .out5(decoder_6_out5), .out6(decoder_6_out6), .out7(decoder_6_out7),
    .out8(decoder_6_out8), .out9(decoder_6_out9), .out10(decoder_6_out10), .out11(decoder_6_out11),
    .out12(decoder_6_out12), .out13(decoder_6_out13), .out14(decoder_6_out14), .sel(multiplexer_19_out));  // open: out15
  Decoder #(.enable("false"), .select(4)) decoder_7 (
    .out2(decoder_7_out2), .out4(decoder_7_out4), .out6(decoder_7_out6), .out10(decoder_7_out10), .sel(icode));  // open: out0, out1, out3, out5, out7, out8, out9, out11, out12, out13, out14, out15
  or or_3 (or_3_out, decoder_7_out2, decoder_7_out4, decoder_7_out6, decoder_7_out10);
  Decoder #(.enable("false"), .select(4)) decoder_8 (
    .out4(decoder_8_out4), .out5(decoder_8_out5), .out6(decoder_8_out6), .out10(decoder_8_out10),
    .out11(decoder_8_out11), .sel(icode));  // open: out0, out1, out2, out3, out7, out8, out9, out12, out13, out14, out15
  Multiplexer #(.width(4)) multiplexer_18 (.in0(4'b1111), .in1(srcA), .out(multiplexer_18_out), .sel(or_3_out));
  or or_4 (or_4_out, decoder_8_out4, decoder_8_out5, decoder_8_out6, decoder_8_out10, decoder_8_out11);
  Multiplexer #(.width(4)) multiplexer_19 (.in0(4'b1111), .in1(srcB), .out(multiplexer_19_out), .sel(or_4_out));

  // Other names for the same wires on the sheet: ln = load_next_in

  // Notes on the sheet:
  //   default to f
  //   second write port is below
  //   this circuit is both DECODE and WRITE BACK. it contains the register file
  //   W1
  //   default to f
  //   W2
  //   tunnel
  //   rax
  //   (0)
  //   rcx
  //   (1)
  //   rdx
  //   (2)
  //   rbx
  //   (3)
  //   rsp
  //   (4)
  //   rbp
  //   (5)
  //   rsi
  //   (6)
  //   rdi
  //   (7)
  //   r8
  //   (8)
  //   r9
  //   (9)
  //   r10
  //   (10)
  //   r11
  //   (11)
  //   r12
  //   (12)
  //   r13
  //   (13)
  //   r14
  //   (14)
  //   R1
  //   R2
  //   default to f
  //   default to f
endmodule

module set_sources_and_destinations (
  input  [3:0] icode,
  input  [3:0] rA,
  input  [3:0] rB,
  output [3:0] srcA,
  output [3:0] srcB,
  output [3:0] dstE,
  output [3:0] dstM
);

  Multiplexer #(.select(4), .width(4)) multiplexer_1 (
    .in0(4'b1111), .in1(4'b1111), .in2(rA), .in3(4'b1111), .in4(rA), .in5(4'b1111), .in6(rA), .in7(4'b1111),
    .in10(rA), .in11(4'b1111), .out(srcA), .sel(icode));  // open: in8, in9, in12, in13, in14, in15
  Multiplexer #(.select(4), .width(4)) multiplexer_2 (
    .in0(4'b1111), .in1(4'b1111), .in2(4'b1111), .in3(4'b1111), .in4(rB), .in5(rB), .in6(rB), .in7(4'b1111),
    .in10(4'b0100), .in11(4'b0100), .out(srcB), .sel(icode));  // open: in8, in9, in12, in13, in14, in15
  Multiplexer #(.select(4), .width(4)) multiplexer_3 (
    .in0(4'b1111), .in1(4'b1111), .in2(rB), .in3(rB), .in4(4'b1111), .in5(4'b1111), .in6(rB), .in7(4'b1111),
    .in10(4'b0100), .in11(4'b0100), .out(dstE), .sel(icode));  // open: in8, in9, in12, in13, in14, in15
  Multiplexer #(.select(4), .width(4)) multiplexer_4 (
    .in0(4'b1111), .in1(4'b1111), .in2(4'b1111), .in3(4'b1111), .in4(4'b1111), .in5(rA), .in6(4'b1111),
    .in7(4'b1111), .in10(4'b1111), .in11(rA), .out(dstM), .sel(icode));  // open: in8, in9, in12, in13, in14, in15

  // Notes on the sheet:
  //   0xF
  //   %rsp
endmodule

module EXECUTE (
  input  count12,
  input  [3:0] icode,
  input  [3:0] ifun,
  input  [63:0] valA,
  input  clk,
  input  [63:0] valC,
  input  [63:0] valB,
  output ZF,
  output SF,
  output OverF,
  output cond_out,
  output [63:0] valE,
  output [63:0] valE_for_memory
);

  wire and_1_out, and_3_out, decoder_1_out11, not_1_out, not_2_out;
  wire [3:0] multiplexer_3_out;
  wire [63:0] adder_1_out, and_2_out, multiplexer_1_out, multiplexer_2_out, subtractor_1_out, xor_1_out;

  Multiplexer #(.select(4), .width(64)) multiplexer_1 (
    .in0({64{1'b0}}), .in1({64{1'b0}}), .in2(valA), .in3(valC), .in4(valC), .in5(valC), .in6(valA),
    .in7({64{1'b0}}), .in8({64{1'b0}}), .in9({64{1'b0}}), .in10(64'hfffffffffffffff8), .in11(64'h8),
    .in12({64{1'b0}}), .in13({64{1'b0}}), .in14({64{1'b0}}), .in15({64{1'b0}}), .out(multiplexer_1_out),
    .sel(icode));
  Multiplexer #(.select(4), .width(64)) multiplexer_2 (
    .in0({64{1'b0}}), .in1({64{1'b0}}), .in2({64{1'b0}}), .in3({64{1'b0}}), .in4(valB), .in5(valB),
    .in6(valB), .in7({64{1'b0}}), .in8({64{1'b0}}), .in9({64{1'b0}}), .in10(valB), .in11(valB),
    .in12({64{1'b0}}), .in13({64{1'b0}}), .in14({64{1'b0}}), .in15({64{1'b0}}), .out(multiplexer_2_out),
    .sel(icode));
  not not_1 (not_1_out, icode[0]);
  and and_1 (and_1_out, not_1_out, icode[1], icode[2], not_2_out);
  not not_2 (not_2_out, icode[3]);
  Adder #(.width(64)) adder_1 (.a(multiplexer_1_out), .b(multiplexer_2_out), .out(adder_1_out));  // open: cin, cout
  Subtractor #(.width(64)) subtractor_1 (
    .a(multiplexer_2_out), .b(multiplexer_1_out), .out(subtractor_1_out));  // open: bin, bout
  assign and_2_out = multiplexer_1_out & multiplexer_2_out;  // AND_Gate and_2, 64 bits wide
  assign xor_1_out = multiplexer_1_out ^ multiplexer_2_out;  // XOR_Gate xor_1, 64 bits wide
  Multiplexer #(.width(4)) multiplexer_3 (.in0(4'b0000), .in1(ifun), .out(multiplexer_3_out), .sel(and_1_out));
  Decoder #(.enable("false"), .select(4)) decoder_1 (
    .out11(decoder_1_out11), .sel(icode));  // open: out0, out1, out2, out3, out4, out5, out6, out7, out8, out9, out10, out12, out13, out14, out15
  Multiplexer #(.select(4), .width(64)) multiplexer_4 (
    .in0(adder_1_out), .in1(subtractor_1_out), .in2(and_2_out), .in3(xor_1_out), .in4(adder_1_out),
    .in5(adder_1_out), .in6(adder_1_out), .in7(adder_1_out), .in8(adder_1_out), .in9(adder_1_out),
    .in10(adder_1_out), .in11(adder_1_out), .in12(adder_1_out), .in13(adder_1_out), .in14(adder_1_out),
    .in15(adder_1_out), .out(valE), .sel(multiplexer_3_out));
  and and_3 (and_3_out, and_1_out, count12);
  Multiplexer #(.width(64)) multiplexer_5 (.in0(valE), .in1(valB), .out(valE_for_memory), .sel(decoder_1_out11));
  cc_registers cc_registers_1 (
    .ifun(ifun), .ValA(valA), .ValB(valB), .clock(clk), .Enable(and_3_out), .ValE(valE), .zero_flag(ZF),
    .sign_flag(SF), .overflow_flag(OverF));
  cond cond_1 (.ZF(ZF), .SF(SF), .OverF(OverF), .ifunc(ifun), .Cond_Out(cond_out));

  // Notes on the sheet:
  //   -8
  //   8
  //   0
  //   0
  //   set CC only when icode = 6
  //   add=0, sub=1, and=2, xor=3, add for rest
  //   implement addq, subq, andq, xorq, and MUX
  //   enable bit for CC registers & ALU MUX
  //   icode
  //   valB
  //   pop
endmodule

module cc_registers (
  input  clock,
  input  Enable,
  input  [63:0] ValE,
  input  [63:0] ValA,
  input  [63:0] ValB,
  input  [3:0] ifun,
  output zero_flag,
  output sign_flag,
  output overflow_flag
);

  wire and_1_out, and_2_out, comparator_1_lt, comparator_2_lt, comparator_3_eq, comparator_3_lt,
       decoder_1_out0, decoder_1_out1, multiplexer_1_out, multiplexer_2_out, multiplexer_3_out, not_1_out,
       or_1_out, xor_1_out, xor_2_out;

  Decoder #(.enable("false"), .select(4)) decoder_1 (
    .out0(decoder_1_out0), .out1(decoder_1_out1), .sel(ifun));  // open: out2, out3, out4, out5, out6, out7, out8, out9, out10, out11, out12, out13, out14, out15
  Comparator #(.width(64)) comparator_1 (.a(ValA), .b({64{1'b0}}), .lt(comparator_1_lt));  // open: gt, eq
  Comparator #(.width(64)) comparator_2 (.a(ValB), .b({64{1'b0}}), .lt(comparator_2_lt));  // open: gt, eq
  xor xor_1 (xor_1_out, comparator_1_lt, comparator_2_lt);
  Comparator #(.width(64)) comparator_3 (
    .a(ValE), .b({64{1'b0}}), .eq(comparator_3_eq), .lt(comparator_3_lt));  // open: gt
  xor xor_2 (xor_2_out, comparator_3_lt, comparator_2_lt);
  not not_1 (not_1_out, xor_1_out);
  and and_1 (and_1_out, xor_2_out, decoder_1_out0, not_1_out);
  and and_2 (and_2_out, xor_2_out, decoder_1_out1, xor_1_out);
  Register #(.width(1)) Zero_Flag_ZF (.D(multiplexer_1_out), .clk(clock), .Q(zero_flag));  // open: en, clr
  Multiplexer multiplexer_1 (.in0(zero_flag), .in1(comparator_3_eq), .out(multiplexer_1_out), .sel(Enable));
  Register #(.width(1)) Sign_Flag_SF (.D(multiplexer_2_out), .clk(clock), .Q(sign_flag));  // open: en, clr
  Multiplexer multiplexer_2 (.in0(sign_flag), .in1(comparator_3_lt), .out(multiplexer_2_out), .sel(Enable));
  Register #(.width(1)) Overflow_Flag_OF (.D(multiplexer_3_out), .clk(clock), .Q(overflow_flag));  // open: en, clr
  Multiplexer multiplexer_3 (.in0(overflow_flag), .in1(or_1_out), .out(multiplexer_3_out), .sel(Enable));
  or or_1 (or_1_out, and_1_out, and_2_out);

  // Other names for the same wires on the sheet: clk = clock

  // Notes on the sheet:
  //   sub
  //   add
  //   valA valB same
  //   valA valB different
  //   valE valB different
endmodule

module cond (
  input  ZF,
  input  SF,
  input  OverF,
  input  [3:0] ifunc,
  output Cond_Out
);

  wire not_1_out, not_2_out, not_3_out, or_1_out, xor_1_out, xor_2_out;

  xor xor_1 (xor_1_out, ZF, SF);
  xor xor_2 (xor_2_out, SF, OverF);
  or or_1 (or_1_out, xor_1_out, OverF);
  not not_1 (not_1_out, ZF);
  not not_2 (not_2_out, xor_2_out);
  not not_3 (not_3_out, or_1_out);
  Multiplexer #(.select(4)) multiplexer_1 (
    .in0(1'b1), .in1(or_1_out), .in2(xor_1_out), .in3(ZF), .in4(not_1_out), .in5(not_2_out), .in6(not_3_out),
    .in7(1'b0), .in8(1'b0), .in9(1'b0), .in10(1'b0), .in11(1'b0), .in12(1'b0), .in13(1'b0), .in14(1'b0),
    .in15(1'b0), .out(Cond_Out), .sel(ifunc));

  // Notes on the sheet:
  //   ifunc = 0, jmp
  //   ifunc = 1, jle
  //   ifunc = 2, jl
  //   ifunc = 3, je
  //   ifunc = 4, jne
  //   ifunc = 5, jge
  //   ifunc = 6, jg
  //   jge true if ~(SF ^ OF)
endmodule

module MEMORY (
  input  read_enable,
  input  clk,
  input  write_enable,
  input  [63:0] mem_data,
  input  [63:0] mem_address,
  output [63:0] valM
);

  wire and_1_out, and_2_out, and_3_out, and_4_out, and_5_out, and_6_out, and_7_out, and_8_out,
       decoder_1_out0, decoder_1_out1, decoder_1_out2, decoder_1_out3, decoder_1_out4, decoder_1_out5,
       decoder_1_out6, decoder_1_out7, or_1_out;
  wire [2:0] c, register_2_q;
  wire [7:0] multiplexer_2_out, multiplexer_3_out, multiplexer_4_out, multiplexer_5_out, multiplexer_6_out,
       multiplexer_7_out, multiplexer_8_out, multiplexer_9_out, multiplexer_10_out, ram_1_dout;
  wire [11:0] adder_1_out;
  wire [63:0] multiplexer_1_out, register_1_q;

  Adder #(.width(12)) adder_1 (.a(register_1_q[11:0]), .b({{9{1'b0}}, c}), .out(adder_1_out));  // open: cin, cout
  RAM #(.addrWidth(12)) ram_1 (
    .addr(adder_1_out), .we(write_enable), .clk(clk), .din(multiplexer_2_out), .dout(ram_1_dout));  // open: oe
  or or_1 (or_1_out, write_enable, read_enable);
  Register #(.width(64)) register_1 (.D(multiplexer_1_out), .clk(clk), .Q(register_1_q));  // open: en, clr
  Multiplexer #(.width(64)) multiplexer_1 (
    .in0(mem_address), .in1(register_1_q), .out(multiplexer_1_out), .sel(write_enable));
  Counter #(.max('h7), .width(3)) counter_1 (.count(or_1_out), .clk(clk), .Q(c));  // open: clr, load, up, D, carry
  Register #(.width(3)) register_2 (.D(c), .clk(clk), .Q(register_2_q));  // open: en, clr
  Multiplexer #(.select(3), .width(8)) multiplexer_2 (
    .in0(mem_data[7:0]), .in1(mem_data[15:8]), .in2(mem_data[23:16]), .in3(mem_data[31:24]),
    .in4(mem_data[39:32]), .in5(mem_data[47:40]), .in6(mem_data[55:48]), .in7(mem_data[63:56]),
    .out(multiplexer_2_out), .sel(c));
  Decoder #(.enable("false"), .select(3)) decoder_1 (
    .out0(decoder_1_out0), .out1(decoder_1_out1), .out2(decoder_1_out2), .out3(decoder_1_out3),
    .out4(decoder_1_out4), .out5(decoder_1_out5), .out6(decoder_1_out6), .out7(decoder_1_out7),
    .sel(register_2_q));
  and and_1 (and_1_out, read_enable, decoder_1_out0);
  and and_2 (and_2_out, read_enable, decoder_1_out1);
  and and_3 (and_3_out, read_enable, decoder_1_out2);
  and and_4 (and_4_out, read_enable, decoder_1_out3);
  and and_5 (and_5_out, read_enable, decoder_1_out4);
  and and_6 (and_6_out, read_enable, decoder_1_out5);
  and and_7 (and_7_out, read_enable, decoder_1_out6);
  and and_8 (and_8_out, read_enable, decoder_1_out7);
  Register register_3 (.D(multiplexer_3_out), .clk(clk), .Q(valM[7:0]));  // open: en, clr
  Multiplexer #(.width(8)) multiplexer_3 (.in0(valM[7:0]), .in1(ram_1_dout), .out(multiplexer_3_out), .sel(and_1_out));
  Register register_4 (.D(multiplexer_4_out), .clk(clk), .Q(valM[15:8]));  // open: en, clr
  Multiplexer #(.width(8)) multiplexer_4 (.in0(valM[15:8]), .in1(ram_1_dout), .out(multiplexer_4_out), .sel(and_2_out));
  Register register_5 (.D(multiplexer_5_out), .clk(clk), .Q(valM[23:16]));  // open: en, clr
  Multiplexer #(.width(8)) multiplexer_5 (
    .in0(valM[23:16]), .in1(ram_1_dout), .out(multiplexer_5_out), .sel(and_3_out));
  Register register_6 (.D(multiplexer_6_out), .clk(clk), .Q(valM[31:24]));  // open: en, clr
  Multiplexer #(.width(8)) multiplexer_6 (
    .in0(valM[31:24]), .in1(ram_1_dout), .out(multiplexer_6_out), .sel(and_4_out));
  Register register_7 (.D(multiplexer_7_out), .clk(clk), .Q(valM[39:32]));  // open: en, clr
  Multiplexer #(.width(8)) multiplexer_7 (
    .in0(valM[39:32]), .in1(ram_1_dout), .out(multiplexer_7_out), .sel(and_5_out));
  Register register_8 (.D(multiplexer_8_out), .clk(clk), .Q(valM[47:40]));  // open: en, clr
  Multiplexer #(.width(8)) multiplexer_8 (
    .in0(valM[47:40]), .in1(ram_1_dout), .out(multiplexer_8_out), .sel(and_6_out));
  Register register_9 (.D(multiplexer_9_out), .clk(clk), .Q(valM[55:48]));  // open: en, clr
  Multiplexer #(.width(8)) multiplexer_9 (
    .in0(valM[55:48]), .in1(ram_1_dout), .out(multiplexer_9_out), .sel(and_7_out));
  Register register_10 (.D(multiplexer_10_out), .clk(clk), .Q(valM[63:56]));  // open: en, clr
  Multiplexer #(.width(8)) multiplexer_10 (
    .in0(valM[63:56]), .in1(ram_1_dout), .out(multiplexer_10_out), .sel(and_8_out));

  // Other names for the same wires on the sheet: read = read_enable; wrt = write_enable

  // Notes on the sheet:
  //   RAM
  //   one cycle off
  //   compensation
endmodule

module set_data_and_address (
  input  [3:0] icode,
  input  [63:0] valE,
  input  [63:0] valA,
  input  [7:0] ct,
  output read,
  output write,
  output [63:0] address,
  output [63:0] data
);

  wire decoder_1_out4, decoder_1_out5, decoder_1_out10, decoder_1_out11, decoder_2_out14, decoder_2_out15,
       decoder_2_out16, decoder_2_out17, decoder_2_out18, decoder_2_out19, decoder_2_out20, decoder_2_out21,
       decoder_3_out4, decoder_3_out5, decoder_3_out10, decoder_3_out11, or_1_out, or_2_out, or_3_out,
       or_4_out, or_5_out;

  Decoder #(.enable("false"), .select(4)) decoder_1 (
    .out4(decoder_1_out4), .out5(decoder_1_out5), .out10(decoder_1_out10), .out11(decoder_1_out11),
    .sel(icode));  // open: out0, out1, out2, out3, out6, out7, out8, out9, out12, out13, out14, out15
  or or_1 (or_1_out, decoder_1_out10, decoder_1_out4, decoder_1_out5, decoder_1_out11);
  or or_2 (or_2_out, decoder_1_out4, decoder_1_out10);
  Multiplexer #(.width(64)) multiplexer_1 (.in1(valE), .out(address), .sel(or_1_out));  // open: in0
  Multiplexer #(.width(64)) multiplexer_2 (.in1(valA), .out(data), .sel(or_2_out));  // open: in0
  Decoder #(.enable("false"), .select(5)) decoder_2 (
    .out14(decoder_2_out14), .out15(decoder_2_out15), .out16(decoder_2_out16), .out17(decoder_2_out17),
    .out18(decoder_2_out18), .out19(decoder_2_out19), .out20(decoder_2_out20), .out21(decoder_2_out21),
    .sel(ct[4:0]));  // open: out0, out1, out2, out3, out4, out5, out6, out7, out8, out9, out10, out11, out12, out13, out22, out23, out24, out25, out26, out27, out28, out29, out30, out31
  Decoder #(.enable("false"), .select(4)) decoder_3 (
    .out4(decoder_3_out4), .out5(decoder_3_out5), .out10(decoder_3_out10), .out11(decoder_3_out11),
    .sel(icode));  // open: out0, out1, out2, out3, out6, out7, out8, out9, out12, out13, out14, out15
  or or_3 (or_3_out, decoder_3_out4, decoder_3_out10);
  or or_4 (or_4_out, decoder_2_out14, decoder_2_out15, decoder_2_out16, decoder_2_out17, decoder_2_out18, decoder_2_out19, decoder_2_out20, decoder_2_out21);
  or or_5 (or_5_out, decoder_3_out5, decoder_3_out11);
  and and_1 (write, or_3_out, or_4_out);
  and and_2 (read, or_4_out, or_5_out);

  // Notes on the sheet:
  //   write signal
  //   mrmovq = read
  //   rmmovq = write
  //   popq = read
  //   pushq = write
  //   read signal
endmodule

module UPDATE (
  input  [11:0] valP,
  input  [63:0] valC,
  input  Cnd,
  input  [3:0] icode,
  output [11:0] new_pc
);

  wire and_1_out, decoder_1_out7;

  Multiplexer #(.width(12)) multiplexer_1 (.in0(valP), .in1(valC[11:0]), .out(new_pc), .sel(and_1_out));
  and and_1 (and_1_out, Cnd, decoder_1_out7);
  Decoder #(.enable("false"), .select(4)) decoder_1 (
    .out7(decoder_1_out7), .sel(icode));  // open: out0, out1, out2, out3, out4, out5, out6, out8, out9, out10, out11, out12, out13, out14, out15
endmodule
